# Fritzing sketch L298-RC-Car (saved by Fritzing 0.9.4)

parts:
  M1 = TP4056 Module [part_number=HW-107]
  M2 = TP4056 Module [part_number=HW-107]
  M3 = TP4056 Module [part_number=HW-107]
  BAT1 = Battery Holders [package=lipo-1100mAh]
  BAT2 = Battery Holders [package=lipo-1100mAh]
  BAT3 = Battery Holders [package=lipo-1100mAh]
  D4 = Schottky Diode [part_number=1N5817 package="Melf DO-213 AB [SMD]"]
  D5 = Schottky Diode [part_number=1N5817 package="Melf DO-213 AB [SMD]"]
  D6 = Schottky Diode [part_number=1N5817 package="Melf DO-213 AB [SMD]"]
  D7 = Schottky Diode [part_number=1N5817 package="Melf DO-213 AB [SMD]"]
  L298N1 = L298N DC motor driver
  M4 = MT3608 Module
  M5 = MT3608 Module
  L298N2 = L298N DC motor driver
  M7 = DC Motor  # not connected
  M8 = DC Motor
  M9 = DC Motor
  M10 = DC Motor
  MCU1 = Raspberry Pi Zero

nets:
  N1: M1.pin1, M2.pin1, M3.pin1, M4.pin1, M5.pin1
  N2: M1.pin3, BAT1.-
  N3: M1.pin4, BAT1.+
  N4: M1.pin5, D6.anode
  N5: M1.pin6, M2.pin6, M3.pin6, D7.anode
  N6: M2.pin3, BAT3.-
  N7: M2.pin4, BAT3.+
  N8: M2.pin5, D5.anode
  N9: M3.pin3, BAT2.-
  N10: M3.pin4, BAT2.+
  N11: M3.pin5, D4.anode
  N12: D4.cathode, D5.cathode, D6.cathode, D7.cathode, M4.pin2, M5.pin2
  N13: L298N1.OUT1, M10.pin_2
  N14: L298N1.OUT2, M10.pin_1
  N15: L298N1.OUT3, M9.pin_1
  N16: L298N1.OUT4, M9.pin_2
  12V: L298N1.12V, M4.pin3, L298N2.12V
  GND: L298N1.GND, M4.pin4, L298N2.GND
  N17: M5.pin3, MCU1.pin_4
  N18: M5.pin4, MCU1.pin_6, MCU1.pin_39
  N19: L298N2.OUT1, M8.pin_1
  N20: L298N2.OUT2, M8.pin_2

notes:
  +8V
  +5V
  +4.6V on charging
  +3 - 3.8V on battery

custom parts:
  TP4056 Module: TP4056 Lithium Battery Charge Management Module Links: TP4056 website
  L298N DC motor driver: 2x DC motor driver with 78M05 positive voltage regulator (7..35 V) L298N: max 46 V, 2 A Set 5 V Enable jumper to enable 5 V regultor (needed for the L298N) and +5 V output at screw terminal or supply external +5 V at screw terminal Set ENA and/or ENB to +5 V to enable motor permanently or supply ENA and/or ENB with PWM signal IN1 and IN2 set rotation directory for motor A (OUT1/OUT2) IN2 and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
  MT3608 Module: MT3608 Boost Converter Module Links: Aerosemi MT3608 2A Step Up Converter datasheet
