# Fritzing sketch wifi-therm-batt (saved by Fritzing 0.9.6b)

parts:
  Plain_Vanilla_ESP2 = Plain Vanilla ESP32
  R10 = Resistor [tolerance=±10% resistance=15k power=0.25 package=THT]
  Power_plug_3_6V1 = Power plug
  R11 = Resistor [tolerance=±10% resistance=15k power=0.25 package=THT]
  R12 = Resistor [tolerance=±10% resistance=1M power=0.25 package=THT]
  R13 = Resistor [tolerance=±10% resistance=1M power=0.25 package=THT]
  J3 = single row smd male pin header, 6 pins [form="♂ (male)"]
  Q1 = NPN-Transistor [package="TO92 [THT]"]
  Q2 = NPN-Transistor [package="TO92 [THT]"]
  R14 = Resistor [tolerance=±10% resistance=15k power=0.25 package=THT]
  R15 = Resistor [tolerance=±10% resistance=15k power=0.25 package=THT]
  J4 = single row smd male pin header, 6 pins [form="♂ (male)"]
  J2 = single row smd male pin header, 6 pins [form="♂ (male)" part_number="To the programmer"]
  RHT2 = Humidity and Temperature Sensor RHT03 [part_number=DHT22]
  MH-ET_Live_Minikit_for_ESP1 = MH-ET Live Minikit for ESP32
  RHT3 = Humidity and Temperature Sensor RHT03 [part_number=DHT22]

nets:
  N1: Plain_Vanilla_ESP2.IO34, R12.Pin_0, R13.Pin_0
  N2: Plain_Vanilla_ESP2.GND#21, Power_plug_3_6V1.GND, R12.Pin_1
  N3: Plain_Vanilla_ESP2.EN, R11.Pin_0, J2.pin5
  3.3V: Plain_Vanilla_ESP2.IO16, Plain_Vanilla_ESP2.3.3V, R10.Pin_1, Power_plug_3_6V1.VCC, R11.Pin_1, R13.Pin_1
  N4: Plain_Vanilla_ESP2.IO0, R10.Pin_0, J2.pin6
  N5: Plain_Vanilla_ESP2.TXD, J2.pin4
  N6: Plain_Vanilla_ESP2.RXD, J2.pin3
  N7: Plain_Vanilla_ESP2.GND#34, J2.pin2, RHT2.GND_2
  N8: Plain_Vanilla_ESP2.IO18, RHT2.Data-signal
  N9: Plain_Vanilla_ESP2.IO17, RHT2.Vcc
  N10: J3.pin3, J4.pin3
  N11: J3.pin4, J4.pin4
  N12: J3.pin5, Q1.C
  N13: J3.pin6, Q2.C
  N14: Q1.E, R15.Pin_1, J4.pin5
  N15: Q1.B, R14.Pin_0
  N16: Q2.E, R14.Pin_1, J4.pin6
  N17: Q2.B, R15.Pin_0
  N18: MH-ET_Live_Minikit_for_ESP1.GND, RHT3.GND_2
  N19: MH-ET_Live_Minikit_for_ESP1.IO18, RHT3.Data-signal
  N20: MH-ET_Live_Minikit_for_ESP1.IO17, RHT3.Vcc

notes:
  3.3V Supply for DHT22 by GPIO17
  GND
  RXD < -------- TXD
  TXD -----------> RXD
  EN/RST
  IO0/FLASH
  GND
  TXD
  RXD
  RTS
  DTR
  ESP32 Battery Powered Thermometer
  Reset and Flash by RTS and DTR

custom parts:
  MH-ET Live Minikit for ESP32: MH-ET Live Minikit for ESP32 ( http://mh.nodebb.com/topic/8/mh-et-live-minikit-for-esp32/2/) PCB footprint is invalid.
