# Fritzing sketch wifi-therm-supply (saved by Fritzing 0.9.6b)

parts:
  M1 = TP4056 Module [part_number=HW-107]
  M2 = MT3608 Module
  U1 = LIPO-1000mAh [package=lipo-1000]
  C1 = Capacitor Polarized [part_number="1000 uF" package=cpol-radial-1000uf-63v]
  D1 = SOLAR-IXYS [package=solarbit-12x1]
  U2 = V_REG_LD1117VXX [package=78xxl]
  J3 = female pin header, 3 pins [form="♀ (female)" part_number=KA75330]
  R1 = Resistor [tolerance=±5% resistance=1k package="0603 [SMD]"]
  RHT3 = Humidity and Temperature Sensor RHT03 [part_number=DHT22]
  Plain_Vanilla_ESP3 = Plain Vanilla ESP32
  R14 = Resistor [tolerance=±10% resistance=15k power=0.25 package=THT]
  R15 = Resistor [tolerance=±10% resistance=15k power=0.25 package=THT]
  R16 = Resistor [tolerance=±10% resistance=1M power=0.25 package=THT]
  J4 = single row smd male pin header, 6 pins [form="♂ (male)" part_number="To the programmer"]
  Power_plug_3_6V2 = Power plug  # not connected
  R17 = Resistor [tolerance=±10% power=0.25 resistance=1M package=THT]

nets:
  N1: M1.GND, D1.A
  N2: M1.OUT-#1, M2.pin4
  N3: M1.BAT-, U1.-
  N4: M1.BAT+, U1.+, R1.Pin_0
  N5: M1.OUT-#4, M2.pin3
  N6: M1.VCC, D1.C
  N7: M2.pin1, C1.-, U2.GND, J3.pin3, Plain_Vanilla_ESP3.GND#21, R16.Pin_1
  N8: M2.pin2, C1.+, U2.IN
  N9: U2.OUT, Plain_Vanilla_ESP3.IO16, Plain_Vanilla_ESP3.3.3V, R14.Pin_1, R15.Pin_1
  N10: J3.pin1, R1.Pin_1
  N11: RHT3.Vcc, Plain_Vanilla_ESP3.IO17
  N12: RHT3.Data-signal, Plain_Vanilla_ESP3.IO18
  N13: RHT3.GND_2, Plain_Vanilla_ESP3.GND#34, J4.pin2
  N14: Plain_Vanilla_ESP3.IO34, R16.Pin_0, R17.Pin_0
  N15: Plain_Vanilla_ESP3.EN, R15.Pin_0, J4.pin5
  N16: Plain_Vanilla_ESP3.IO0, R14.Pin_0, J4.pin6
  N17: Plain_Vanilla_ESP3.TXD, J4.pin4
  N18: Plain_Vanilla_ESP3.RXD, J4.pin3

notes:
  3.3V
  2.6 - 4.5 V
  5.5 V
  Solar Panel
  0 - 6 V
  to ESP32 chip reset
  1K resistor create hysteresis 3.23 - 3.50 V
  3.3V Supply for DHT22 by GPIO17
  GND
  RXD < -------- TXD
  TXD -----------> RXD
  EN/RST
  IO0/FLASH

custom parts:
  TP4056 Module: TP4056 Lithium Battery Charge Management Module Links: TP4056 website
  MT3608 Module: MT3608 Boost Converter Module Links: Aerosemi MT3608 2A Step Up Converter datasheet
